# Fritzing sketch CurtainController (saved by Fritzing 0.9.1b)
stripboards: 1

parts:
  Part1 = Arduino Nano (Rev3.0)
  IC1 = L293D [package=THT]
  IC2 = L293D [package=THT]
  J2 = shrouded pin header, 8 pins [form="♂ (shrouded male)"]  # not connected
  J3 = screw terminal, 8 pins

nets (from the schematic view):
  N1: Part1.D2, IC2.Enable_1
  N2: Part1.D3, IC2.In_1
  N3: Part1.D4, IC2.In_2
  N4: Part1.D5, IC1.In_2
  N5: Part1.D6, IC1.In_1
  N6: Part1.D7, IC1.Enable_1
  N7: Part1.D8, IC1.Enable_2
  N8: Part1.D9, IC1.In_3
  N9: Part1.D10, IC1.In_4
  N10: Part1.VIN, IC1.+Vmotor, IC2.+Vmotor
  N11: Part1.5V, IC1.+V, IC2.+V
  N12: Part1.A2, IC2.Enable_2
  N13: Part1.A1, IC2.In_3
  N14: Part1.A0, IC2.In_4
  N15: IC1.Out_1_(_Controlled_by_Enable_1_), J3.pin2
  N16: IC1.Out_2_(_Controlled_by_Enable_1_), J3.pin1
  N17: IC1.Out_3_(_Controlled_by_Enable_2_), J3.pin3
  N18: IC1.Out_4_(_Controlled_by_Enable_2_), J3.pin4
  N19: IC2.Out_1_(_Controlled_by_Enable_1_), J3.pin6
  N20: IC2.Out_2_(_Controlled_by_Enable_1_), J3.pin5
  N21: IC2.Out_3_(_Controlled_by_Enable_2_), J3.pin7
  N22: IC2.Out_4_(_Controlled_by_Enable_2_), J3.pin8
