# Fritzing sketch DrapeRemote (saved by Fritzing 0.9.0b)
stripboards: 1

parts:
  Q1 = PNP-Transistor [package="TO92 [THT]"]
  Q2 = PNP-Transistor [package="TO92 [THT]"]
  Q3 = PNP-Transistor [package="TO92 [THT]"]
  R1 = Resistor [tolerance=±5% resistance=220 package=THT]
  R2 = Resistor [tolerance=±5% resistance=220 package=THT]
  J1 = shrouded pin header, 8 pins [form="♂ (shrouded male)"]
  R3 = Resistor [tolerance=±5% resistance=220 package=THT]
  Part1 = Arduino Pro Mini v13

nets:
  N1: Q1.B, R3.Pin_1
  N2: Q1.C, Q2.C, Q3.C
  N3: Q2.B, R1.Pin_1
  N4: Q3.B, R2.Pin_1
  N5: R1.Pin_0, Part1.D5_PWM
  N6: R2.Pin_0, Part1.D4
  N7: J1.pin2, Part1.D11_PWM/MOSI
  N8: J1.pin3, Part1.D3_PWM
  N9: J1.pin4, Part1.VCC
  N10: J1.pin5, Part1.GND
  N11: J1.pin6, Part1.D2
  N12: J1.pin7, Part1.D13/SCK
  N13: J1.pin8, Part1.D12/MISO
  N14: R3.Pin_0, Part1.D10_PWM/SS

custom parts:
  Arduino Pro Mini v13: It's blue! It's thin! It's the Arduino Pro Mini! SparkFun's minimal design approach to Arduino. This is a 5V Arduino running the 16MHz bootloader. Arduino Pro Mini does not come with connectors populated so that you can solder in any connector or wire with any orientation you need. We recommend first time Arduino users start with the Uno R3. It's a great board that will get you up and running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
