# Fritzing sketch SprinklerController (saved by Fritzing 0.9.0b)
stripboards: 1

parts:
  K2 = Relay [part_number=322170052000 package=THT]
  K1 = Relay [part_number=322170052000 package=THT]
  D2 = Rectifier Diode [part_number=1N4001 package="300 mil [THT]"]
  Q1 = NPN-Transistor [package="TO92 [THT]"]
  J1 = screw terminal, 3 pins
  J2 = screw terminal, 3 pins
  AC = screw terminal, 3 pins
  Q2 = NPN-Transistor [package="TO92 [THT]"]
  D3 = Rectifier Diode [part_number=1N4001 package="300 mil [THT]"]

nets:
  N1: K2.COIL1, D3.cathode
  N2: K2.C, K1.B, AC.pin1
  N3: K2.COIL2, Q1.C, D3.anode
  N4: K2.B, J1.pin1
  N5: K1.COIL1, D2.anode, Q2.C
  N6: K1.C, J2.pin3
  N7: K1.COIL2, D2.cathode
  N8: J1.pin3, J2.pin1, AC.pin3

custom parts:
  Relay: A Finding 3221x000 relay.
