# Fritzing sketch marble_master (saved by Fritzing 0.9.2b)
stripboards: 1

parts:
  Q1 = NPN-Transistor [package="SOT-23 [SMD]"]
  U4 = V_REG_LD1117VXX [package=78xxl]
  C2 = Electrolytic Capacitor [capacitance=470µF package="300 mil [THT, electrolytic]"]
  C1 = Electrolytic Capacitor [capacitance=470µF package="300 mil [THT, electrolytic]"]
  C3 = Ceramic Capacitor [capacitance=100nF package="100 mil [THT, multilayer]"]
  U2 = Optocoupler [package=THT]
  U1 = ESP8266 WiFi Module [part_number=ESP8266]
  C4 = Ceramic Capacitor [capacitance=100nF package="100 mil [THT, multilayer]"]
  R1 = Resistor [tolerance=±5% resistance=220 package=THT]
  M1 = DC Motor
  R2 = Resistor [tolerance=±5% resistance=10k package=THT]

nets:
  GND: Q1.2, U4.GND, C2.-, C1.-, C3.0, U2.Pin_4, U1.GND, C4.0
  N1: Q1.0, U2.Pin_5, R2.Pin_1
  N2: Q1.1, M1.pin_2
  N3: U4.OUT, C2.+, C3.1, U1.VCC, U1.CH_PD, R1.Pin_0
  12V: U4.IN, C1.+, C4.1, M1.pin_1, R2.Pin_0
  N4: U2.Pin_1, R1.Pin_1
  N5: U2.Pin_2, U1.GPIO_0

custom parts:
  ESP8266 WiFi Module: Generic WiFi Module based on the ESP8266 with onboard PCB antenna and UART communications
